// Logisim project CS1409_U201414795_王卓焱_cpu.circ as structural Verilog: 4 circuits, main circuit main
module main (
);

  wire Acount, and_2_out, Bcount, clk, clk2, clu_1_branch, clu_1_memwrite, clu_1_regwrite, comparator_1_eq,
       comparator_1_gt, comparator_1_lt, equal, halt, Mcount, multiplexer_1_out, not_1_out, others, r1out,
       syscall;
  wire [1:0] alusrc, clu_1_memtoreg, jp, regdst;
  wire [3:0] clu_1_aluc, multiplexer_5_out_2;
  wire [4:0] r1reg, wrin;
  wire [25:0] address;
  wire [27:0] multiplexer_5_out;
  wire [31:0] a0, adder_1_out, adder_2_out, adder_3_out, adder_4_out, alu_1_result, bit_extender_1_out,
       bit_extender_2_out, bit_extender_3_out, bit_extender_4_out, bit_extender_5_out, bit_extender_6_out,
       counter_1_q, counter_2_q, counter_3_q, counter_4_q, counter_5_q, counter_6_q, jr_out,
       multiplexer_3_out, multiplexer_4_out, multiplexer_9_out, out_reg2, ram_1_data, register_1_q, s0, s1,
       shifter_1_out, v0, Yin;
  wire [31:26] rom_1_data;

  not not_1 (not_1_out, equal);
  Clock clock_1 (.out(clk2));
  Counter #(.width(32), .max('hffffffff)) counter_1 (
    .D(32'h1), .Q(counter_1_q), .clk(clk));  // open: load, count, carry, clr
  assign bit_extender_1_out = {{31{1'b0}}, halt};  // Bit_Extender bit_extender_1
  Multiplexer #(.enable("false")) multiplexer_1 (
    .in0(equal), .in1(not_1_out), .out(multiplexer_1_out), .sel(clu_1_branch));
  Multiplexer #(.enable("false")) multiplexer_2 (.in0(clk2), .in1(1'b0), .out(clk), .sel(halt));
  Comparator #(.width(32), .mode("unsigned")) comparator_1 (
    .a(v0), .b(32'ha), .gt(comparator_1_gt), .eq(comparator_1_eq), .lt(comparator_1_lt));
  Multiplexer #(.width(32), .enable("false")) multiplexer_3 (
    .in0(adder_2_out), .in1(adder_3_out), .out(multiplexer_3_out), .sel(multiplexer_1_out));
  Adder #(.width(32)) adder_1 (.a(counter_1_q), .b(bit_extender_1_out), .out(adder_1_out));  // open: cin, cout
  // Probe on adder_1_out
  and and_1 (halt, syscall, comparator_1_eq);
  Counter #(.width(32), .max('hffffffff), .trigger("falling")) counter_2 (
    .count(jp[1]), .Q(counter_2_q), .clk(clk));  // open: load, D, carry, clr
  // Probe on counter_2_q
  Multiplexer #(.select(2), .width(32), .enable("false")) multiplexer_4 (
    .in0(adder_2_out), .in1(multiplexer_3_out), .in2({adder_2_out[31:28], address, 2'b00}), .in3(jr_out),
    .out(multiplexer_4_out), .sel(jp));
  Hex_Digit_Display hex_digit_display_1 (.value(multiplexer_5_out_2));  // open: dp
  Multiplexer #(.width(32), .enable("false")) multiplexer_5 (
    .in0(a0), .out({multiplexer_5_out_2, multiplexer_5_out}), .sel(and_2_out));  // open: in1
  and and_2 (and_2_out, comparator_1_gt, comparator_1_lt);
  Register #(.width(32)) register_1 (.D(multiplexer_4_out), .Q(register_1_q), .clk(clk));  // open: en, clr
  Hex_Digit_Display hex_digit_display_2 (.value(multiplexer_5_out[23:20]));  // open: dp
  Hex_Digit_Display hex_digit_display_3 (.value(multiplexer_5_out[27:24]));  // open: dp
  // Probe on a0
  Multiplexer #(.width(5), .enable("false")) multiplexer_6 (
    .in0(address[25:21]), .in1(address[20:16]), .out(r1reg), .sel(r1out));
  Adder #(.width(32)) adder_2 (.a(register_1_q), .b(32'h4), .out(adder_2_out), .cin(1'b0));  // open: cout
  Hex_Digit_Display hex_digit_display_4 (.value(multiplexer_5_out[19:16]));  // open: dp
  Hex_Digit_Display hex_digit_display_5 (.value(multiplexer_5_out[15:12]));  // open: dp
  Counter #(.width(32), .max('hffffffff), .trigger("falling")) counter_3 (
    .count(Bcount), .Q(counter_3_q), .clk(clk));  // open: load, D, carry, clr
  // Probe on counter_3_q
  Hex_Digit_Display hex_digit_display_6 (.value(multiplexer_5_out[7:4]));  // open: dp
  Hex_Digit_Display hex_digit_display_7 (.value(multiplexer_5_out[11:8]));  // open: dp
  ROM #(.addrWidth(10), .dataWidth(32)) rom_1 (.addr(register_1_q[11:2]), .data({rom_1_data, address}));  // open: sel
  Hex_Digit_Display hex_digit_display_8 (.value(multiplexer_5_out[3:0]));  // open: dp
  CLU clu_1 (
    .op(rom_1_data), .fc(address[5:0]), .MemtoReg(clu_1_memtoreg), .syscallout(syscall), .RegDst(regdst),
    .MemWrite(clu_1_memwrite), .Branch(clu_1_branch), .ALUSrc(alusrc), .RegWrite(clu_1_regwrite),
    .ALUC(clu_1_aluc), .pcnxt(jp), .r1out(r1out), .Bcount(Bcount), .Aout(Acount), .mout(Mcount),
    .others(others));
  assign bit_extender_2_out = {{16{1'b0}}, address[15:0]};  // Bit_Extender bit_extender_2
  assign bit_extender_3_out = {{16{address[15]}}, address[15:0]};  // Bit_Extender bit_extender_3
  assign bit_extender_4_out = {{16{1'b0}}, address[15:0]};  // Bit_Extender bit_extender_4
  assign bit_extender_5_out = {{27{1'b0}}, address[10:6]};  // Bit_Extender bit_extender_5
  // Probe on counter_4_q
  Counter #(.width(32), .max('hffffffff)) counter_4 (
    .count(Acount), .Q(counter_4_q), .clk(clk));  // open: load, D, carry, clr
  regfile regfile_1 (
    .Reg1_num(r1reg), .Reg2(address[20:16]), .Write_Reg_num(wrin), .Din(multiplexer_9_out),
    .Write_Enable(clu_1_regwrite), .Clock(clk), .Reg1(jr_out), .Reg2_2(out_reg2), .a0(a0), .s0(s0), .s1(s1),
    .v0(v0));  // open: reg31
  ALU alu_1 (
    .AluOP(clu_1_aluc), .X(jr_out), .Equal(equal), .Result(alu_1_result), .Y(Yin));  // open: Signed_Overflow, Result_2, UnSigned_Overflow
  Shifter #(.width(32)) shifter_1 (.in(bit_extender_2_out), .\dist (5'b00010), .out(shifter_1_out));
  // Probe on alu_1_result
  Adder #(.width(32)) adder_3 (.a(shifter_1_out), .b(adder_2_out), .out(adder_3_out), .cin(1'b0));  // open: cout
  Multiplexer #(.select(2), .width(32), .enable("false")) multiplexer_7 (
    .in0(out_reg2), .in1(bit_extender_3_out), .in2(bit_extender_4_out), .in3(bit_extender_5_out), .out(Yin),
    .sel(alusrc));
  // Probe on counter_5_q
  Counter #(.width(32), .max('hffffffff)) counter_5 (
    .count(Mcount), .Q(counter_5_q), .clk(clk));  // open: load, D, carry, clr
  RAM #(.addrWidth(10), .dataWidth(32), .bus("separate")) ram_1 (
    .addr(alu_1_result[11:2]), .din(out_reg2), .data(ram_1_data), .str(clu_1_memwrite), .clk(clk), .ld(1'b1));  // open: sel, clr
  Multiplexer #(.select(2), .width(5), .enable("false")) multiplexer_8 (
    .in0(address[20:16]), .in1(address[15:11]), .in2({5{1'b1}}), .out(wrin), .sel(regdst));  // open: in3
  assign bit_extender_6_out = {{31{1'b0}}, halt};  // Bit_Extender bit_extender_6
  Counter #(.width(32), .max('hffffffff)) counter_6 (
    .count(others), .Q(counter_6_q), .clk(clk));  // open: load, D, carry, clr
  Adder #(.width(32)) adder_4 (.a(bit_extender_6_out), .b(counter_6_q), .out(adder_4_out));  // open: cin, cout
  // Probe on adder_4_out
  Multiplexer #(.select(2), .width(32), .enable("false")) multiplexer_9 (
    .in0(alu_1_result), .in1(ram_1_data), .in2(adder_2_out), .out(multiplexer_9_out), .sel(clu_1_memtoreg));  // open: in3

  // Other names for the same wires on the sheet: rd[4:0] = address[15:11]; rt[4:0] = address[20:16];
  //   rs[4:0] = address[25:21]

  // Notes on the sheet:
  //   指令量条数
  //   JUMP
  //   branch
  //   contents of rom_1 (hex, n*v repeats v):
  //   20110001 8000c05 20110001 20120002 20130003 8000c09 20110001 20120002 20130003 8000c0d 20110001
  //   20120002 20130003 8000c11 20110001 20120002 20130003 c000cb8 20100001 20110001 118fc0 112020
  //   20020022 c 118882 12200001 8000c15 112020 20020022 c 20110001 118880 112020 20020022 c 12200001
  //   8000c1f 20110001 118fc0 112020 20020022 c 1188c3 112020 20020022 c 118903 112020 20020022 c 118903
  //   112020 20020022 c 118903 112020 20020022 c 118903 112020 20020022 c 118903 112020 20020022 c 118903
  //   112020 20020022 c 118903 112020 20020022 c 20100001 109fc0 139fc3 8021 2012000c 24160003 26100001
  //   3210000f 20080008 20090001 139900 2709825 132020 20020022 c 1094022 1500fff9 22100001 2018000f
  //   2188024 108700 20080008 20090001 139902 2709825 132021 20020022 c 1094022 1500fff9 108702 2c9b022
  //   12c00001 8000c50 4020 1084027 84400 3508ffff 82021 20020022 c 2010ffff 20110000 ae300000 22100001
  //   22310004 ae300000 22100001 22310004 ae300000 22100001 22310004 ae300000 22100001 22310004 ae300000
  //   22100001 22310004 ae300000 22100001 22310004 ae300000 22100001 22310004 ae300000 22100001 22310004
  //   ae300000 22100001 22310004 ae300000 22100001 22310004 ae300000 22100001 22310004 ae300000 22100001
  //   22310004 ae300000 22100001 22310004 ae300000 22100001 22310004 ae300000 22100001 22310004 ae300000
  //   22100001 22310004 22100001 8020 2011003c 8e130000 8e340000 274402a 11000002 ae330000 ae140000
  //   2231fffc 1611fff8 102020 20020022 c 22100004 2011003c 1611fff2 2002000a c 20100000 22100001 102020
  //   20020022 c 22100002 102020 20020022 c 22100003 102020 20020022 c 22100004 102020 20020022 c 22100005
  //   102020 20020022 c 22100006 102020 20020022 c 22100007 102020 20020022 c 22100008 102020 20020022
  //   20020022 c 3e00008
  //   alu
  //   memory
  //   others
endmodule

module IPdeco (
  input  OP1,
  input  OP2,
  input  OP3,
  input  OP4,
  input  OP5,
  input  OP6,
  input  FU1,
  input  FU2,
  input  FU3,
  input  FU4,
  input  FU5,
  input  FU6,
  output NOR,
  output ADD,
  output LW,
  output ADDI,
  output SW,
  output ADDIU,
  output BOE,
  output BNE,
  output ADDU,
  output SLT,
  output AND,
  output SLTI,
  output ANDI,
  output SLTU,
  output JMP,
  output SLL,
  output JAL,
  output SRA,
  output JR,
  output SRL,
  output SYSCALL,
  output SUB,
  output OR,
  output ORI
);

  wire not_1_out, not_2_out, not_3_out, not_4_out, not_5_out, not_6_out, not_7_out, not_8_out, not_9_out,
       not_10_out, not_11_out, not_12_out, not_13_out, not_14_out, not_15_out, not_16_out, not_17_out,
       not_18_out, not_19_out, not_20_out, not_21_out, not_22_out, not_23_out, not_24_out, not_25_out,
       not_26_out, not_27_out, not_28_out, not_29_out, not_30_out, not_31_out, not_32_out, not_33_out,
       not_34_out, not_35_out, not_36_out, not_37_out, not_38_out, not_39_out, not_40_out, not_41_out,
       not_42_out, not_43_out, not_44_out, not_45_out, not_46_out, not_47_out, not_48_out, not_49_out,
       not_50_out, not_51_out, not_52_out, not_53_out, not_54_out, not_55_out, not_56_out, not_57_out,
       not_58_out, not_59_out, not_60_out, not_61_out, not_62_out, not_63_out, not_64_out, not_65_out,
       not_66_out, not_67_out, not_68_out, not_69_out, not_70_out, not_71_out, not_72_out, not_73_out,
       not_74_out, not_75_out, not_76_out, not_77_out, not_78_out, not_79_out, not_80_out, not_81_out,
       not_82_out, not_83_out, not_84_out, not_85_out, not_86_out, not_87_out, not_88_out, not_89_out,
       not_90_out, not_91_out, not_92_out, not_93_out, not_94_out, not_95_out, not_96_out, not_97_out,
       not_98_out, not_99_out, not_100_out, not_101_out, not_102_out, not_103_out, not_104_out, not_105_out,
       not_106_out, not_107_out, not_108_out, not_109_out, not_110_out, not_111_out, not_112_out,
       not_113_out, not_114_out, not_115_out, not_116_out, not_117_out, not_118_out, not_119_out,
       not_120_out, not_121_out, not_122_out, not_123_out, not_124_out, not_125_out, not_126_out,
       not_127_out, not_128_out, not_129_out, not_130_out, not_131_out, not_132_out, not_133_out,
       not_134_out, not_135_out, not_136_out, not_137_out, not_138_out, not_139_out, not_140_out,
       not_141_out, not_142_out, not_143_out, not_144_out, not_145_out, not_146_out, not_147_out,
       not_148_out, not_149_out, not_150_out, not_151_out, not_152_out, not_153_out, not_154_out,
       not_155_out, not_156_out, not_157_out, not_158_out, not_159_out, not_160_out, not_161_out,
       not_162_out, not_163_out, not_164_out, not_165_out, not_166_out, not_167_out, not_168_out,
       not_169_out, not_170_out, not_171_out, not_172_out;

  not not_1 (not_1_out, OP1);
  not not_2 (not_2_out, OP2);
  not not_3 (not_3_out, OP3);
  not not_4 (not_4_out, OP4);
  not not_5 (not_5_out, OP5);
  not not_6 (not_6_out, OP6);
  not not_7 (not_7_out, FU2);
  not not_8 (not_8_out, FU3);
  not not_9 (not_9_out, OP2);
  not not_10 (not_10_out, OP3);
  not not_11 (not_11_out, OP4);
  not not_12 (not_12_out, OP2);
  not not_13 (not_13_out, OP4);
  not not_14 (not_14_out, OP1);
  not not_15 (not_15_out, OP2);
  not not_16 (not_16_out, OP3);
  not not_17 (not_17_out, OP5);
  not not_18 (not_18_out, OP6);
  not not_19 (not_19_out, OP1);
  not not_20 (not_20_out, OP2);
  not not_21 (not_21_out, OP3);
  not not_22 (not_22_out, OP5);
  not not_23 (not_23_out, OP1);
  not not_24 (not_24_out, OP2);
  not not_25 (not_25_out, OP3);
  not not_26 (not_26_out, OP4);
  not not_27 (not_27_out, OP5);
  not not_28 (not_28_out, OP6);
  not not_29 (not_29_out, FU2);
  not not_30 (not_30_out, FU4);
  not not_31 (not_31_out, FU6);
  not not_32 (not_32_out, OP1);
  not not_33 (not_33_out, OP2);
  not not_34 (not_34_out, OP4);
  not not_35 (not_35_out, OP6);
  not not_36 (not_36_out, OP1);
  not not_37 (not_37_out, OP2);
  not not_38 (not_38_out, OP3);
  not not_39 (not_39_out, OP4);
  not not_40 (not_40_out, OP5);
  not not_41 (not_41_out, OP6);
  not not_42 (not_42_out, FU2);
  not not_43 (not_43_out, FU4);
  not not_44 (not_44_out, OP1);
  not not_45 (not_45_out, OP2);
  not not_46 (not_46_out, OP3);
  not not_47 (not_47_out, OP4);
  not not_48 (not_48_out, OP6);
  not not_49 (not_49_out, OP1);
  not not_50 (not_50_out, OP2);
  not not_51 (not_51_out, OP3);
  not not_52 (not_52_out, OP4);
  not not_53 (not_53_out, OP1);
  not not_54 (not_54_out, OP2);
  not not_55 (not_55_out, OP3);
  not not_56 (not_56_out, OP4);
  not not_57 (not_57_out, OP5);
  not not_58 (not_58_out, OP6);
  not not_59 (not_59_out, FU1);
  not not_60 (not_60_out, FU2);
  not not_61 (not_61_out, FU4);
  not not_62 (not_62_out, FU5);
  not not_63 (not_63_out, FU6);
  not not_64 (not_64_out, OP1);
  not not_65 (not_65_out, OP2);
  not not_66 (not_66_out, OP3);
  not not_67 (not_67_out, OP4);
  not not_68 (not_68_out, OP5);
  not not_69 (not_69_out, OP6);
  not not_70 (not_70_out, FU1);
  not not_71 (not_71_out, FU2);
  not not_72 (not_72_out, FU5);
  not not_73 (not_73_out, FU6);
  and and_1 (NOR, not_1_out, not_2_out, not_3_out, not_4_out, not_5_out, not_6_out, FU1, not_7_out, not_8_out, FU4, FU5, FU6);
  and and_2 (LW, OP1, not_9_out, not_10_out, not_11_out, OP5, OP6);
  and and_3 (SW, OP1, not_12_out, OP3, not_13_out, OP5, OP6);
  and and_4 (BOE, not_14_out, not_15_out, not_16_out, OP4, not_17_out, not_18_out);
  and and_5 (BNE, not_19_out, not_20_out, not_21_out, OP4, not_22_out, OP6);
  and and_6 (SLT, not_23_out, not_24_out, not_25_out, not_26_out, not_27_out, not_28_out, FU1, not_29_out, FU3, not_30_out, FU5, not_31_out);
  and and_7 (SLTI, not_32_out, not_33_out, OP3, not_34_out, OP5, not_35_out);
  and and_8 (SLTU, not_36_out, not_37_out, not_38_out, not_39_out, not_40_out, not_41_out, FU1, not_42_out, FU3, not_43_out, FU5, FU6);
  and and_9 (JMP, not_44_out, not_45_out, not_46_out, not_47_out, OP5, not_48_out);
  and and_10 (JAL, not_49_out, not_50_out, not_51_out, not_52_out, OP5, OP6);
  and and_11 (JR, not_53_out, not_54_out, not_55_out, not_56_out, not_57_out, not_58_out, not_59_out, not_60_out, FU3, not_61_out, not_62_out, not_63_out);
  and and_12 (SYSCALL, not_64_out, not_65_out, not_66_out, not_67_out, not_68_out, not_69_out, not_70_out, not_71_out, FU3, FU4, not_72_out, not_73_out);
  not not_74 (not_74_out, OP1);
  not not_75 (not_75_out, OP2);
  not not_76 (not_76_out, OP3);
  not not_77 (not_77_out, OP4);
  not not_78 (not_78_out, OP5);
  not not_79 (not_79_out, OP6);
  not not_80 (not_80_out, FU2);
  not not_81 (not_81_out, FU3);
  not not_82 (not_82_out, FU4);
  not not_83 (not_83_out, FU5);
  not not_84 (not_84_out, FU6);
  not not_85 (not_85_out, OP1);
  not not_86 (not_86_out, OP2);
  not not_87 (not_87_out, OP4);
  not not_88 (not_88_out, OP5);
  not not_89 (not_89_out, OP6);
  not not_90 (not_90_out, OP1);
  not not_91 (not_91_out, OP2);
  not not_92 (not_92_out, OP4);
  not not_93 (not_93_out, OP5);
  not not_94 (not_94_out, OP1);
  not not_95 (not_95_out, OP2);
  not not_96 (not_96_out, OP3);
  not not_97 (not_97_out, OP4);
  not not_98 (not_98_out, OP5);
  not not_99 (not_99_out, OP6);
  not not_100 (not_100_out, FU2);
  not not_101 (not_101_out, FU3);
  not not_102 (not_102_out, FU4);
  not not_103 (not_103_out, FU5);
  not not_104 (not_104_out, OP1);
  not not_105 (not_105_out, OP2);
  not not_106 (not_106_out, OP3);
  not not_107 (not_107_out, OP4);
  not not_108 (not_108_out, OP5);
  not not_109 (not_109_out, OP6);
  not not_110 (not_110_out, FU2);
  not not_111 (not_111_out, FU3);
  not not_112 (not_112_out, FU5);
  not not_113 (not_113_out, FU6);
  not not_114 (not_114_out, OP1);
  not not_115 (not_115_out, OP2);
  not not_116 (not_116_out, OP5);
  not not_117 (not_117_out, OP6);
  not not_118 (not_118_out, OP1);
  not not_119 (not_119_out, OP2);
  not not_120 (not_120_out, OP3);
  not not_121 (not_121_out, OP4);
  not not_122 (not_122_out, OP5);
  not not_123 (not_123_out, OP6);
  not not_124 (not_124_out, FU1);
  not not_125 (not_125_out, FU2);
  not not_126 (not_126_out, FU3);
  not not_127 (not_127_out, FU4);
  not not_128 (not_128_out, FU5);
  not not_129 (not_129_out, FU6);
  not not_130 (not_130_out, OP1);
  not not_131 (not_131_out, OP2);
  not not_132 (not_132_out, OP3);
  not not_133 (not_133_out, OP4);
  not not_134 (not_134_out, OP5);
  not not_135 (not_135_out, OP6);
  not not_136 (not_136_out, FU1);
  not not_137 (not_137_out, FU2);
  not not_138 (not_138_out, FU3);
  not not_139 (not_139_out, FU4);
  not not_140 (not_140_out, OP1);
  not not_141 (not_141_out, OP2);
  not not_142 (not_142_out, OP3);
  not not_143 (not_143_out, OP4);
  not not_144 (not_144_out, OP5);
  not not_145 (not_145_out, OP6);
  not not_146 (not_146_out, FU1);
  not not_147 (not_147_out, FU2);
  not not_148 (not_148_out, FU3);
  not not_149 (not_149_out, FU4);
  not not_150 (not_150_out, FU6);
  not not_151 (not_151_out, OP1);
  not not_152 (not_152_out, OP2);
  not not_153 (not_153_out, OP3);
  not not_154 (not_154_out, OP4);
  not not_155 (not_155_out, OP5);
  not not_156 (not_156_out, OP6);
  not not_157 (not_157_out, FU2);
  not not_158 (not_158_out, FU3);
  not not_159 (not_159_out, FU4);
  not not_160 (not_160_out, FU6);
  not not_161 (not_161_out, OP1);
  not not_162 (not_162_out, OP2);
  not not_163 (not_163_out, OP3);
  not not_164 (not_164_out, OP4);
  not not_165 (not_165_out, OP5);
  not not_166 (not_166_out, OP6);
  not not_167 (not_167_out, FU2);
  not not_168 (not_168_out, FU3);
  not not_169 (not_169_out, FU5);
  not not_170 (not_170_out, OP1);
  not not_171 (not_171_out, OP2);
  not not_172 (not_172_out, OP5);
  and and_13 (ADDI, not_85_out, not_86_out, OP3, not_87_out, not_88_out, not_89_out);
  and and_14 (ADDIU, not_90_out, not_91_out, OP3, not_92_out, not_93_out, OP6);
  and and_15 (ANDI, not_114_out, not_115_out, OP3, OP4, not_116_out, not_117_out);
  and and_16 (ORI, not_170_out, not_171_out, OP3, OP4, not_172_out, OP6);
  and and_17 (ADD, not_74_out, not_75_out, not_76_out, not_77_out, not_78_out, not_79_out, FU1, not_80_out, not_81_out, not_82_out, not_83_out, not_84_out);
  and and_18 (ADDU, not_94_out, not_95_out, not_96_out, not_97_out, not_98_out, not_99_out, FU1, not_100_out, not_101_out, not_102_out, not_103_out, FU6);
  and and_19 (AND, not_104_out, not_105_out, not_106_out, not_107_out, not_108_out, not_109_out, FU1, not_110_out, not_111_out, FU4, not_112_out, not_113_out);
  and and_20 (SLL, not_118_out, not_119_out, not_120_out, not_121_out, not_122_out, not_123_out, not_124_out, not_125_out, not_126_out, not_127_out, not_128_out, not_129_out);
  and and_21 (SRA, not_130_out, not_131_out, not_132_out, not_133_out, not_134_out, not_135_out, not_136_out, not_137_out, not_138_out, not_139_out, FU5, FU6);
  and and_22 (SRL, not_140_out, not_141_out, not_142_out, not_143_out, not_144_out, not_145_out, not_146_out, not_147_out, not_148_out, not_149_out, FU5, not_150_out);
  and and_23 (SUB, not_151_out, not_152_out, not_153_out, not_154_out, not_155_out, not_156_out, FU1, not_157_out, not_158_out, not_159_out, FU5, not_160_out);
  and and_24 (OR, not_161_out, not_162_out, not_163_out, not_164_out, not_165_out, not_166_out, FU1, not_167_out, not_168_out, FU4, not_169_out, FU6);
endmodule

module CLU (
  input  [5:0] op,
  input  [5:0] fc,
  output Aout,
  output others,
  output mout,
  output Bcount,
  output r1out,
  output [1:0] pcnxt,
  output RegWrite,
  output MemWrite,
  output Branch,
  output syscallout,
  output [3:0] ALUC,
  output [1:0] RegDst,
  output [1:0] MemtoReg,
  output [1:0] ALUSrc
);

  wire ipdeco_1_add, ipdeco_1_addi, ipdeco_1_addiu, ipdeco_1_addu, ipdeco_1_and, ipdeco_1_andi, ipdeco_1_boe,
       ipdeco_1_jmp, ipdeco_1_jr, ipdeco_1_nor, ipdeco_1_or, ipdeco_1_ori, ipdeco_1_sll, ipdeco_1_slt,
       ipdeco_1_slti, ipdeco_1_sltu, ipdeco_1_sra, ipdeco_1_srl, ipdeco_1_sub, or_3_out, or_9_out, or_10_out,
       or_12_out;

  IPdeco ipdeco_1 (
    .OP1(op[5]), .OP2(op[4]), .OP3(op[3]), .OP4(op[2]), .OP5(op[1]), .OP6(op[0]), .FU1(fc[5]), .FU2(fc[4]),
    .FU3(fc[3]), .FU4(fc[2]), .FU5(fc[1]), .FU6(fc[0]), .NOR(ipdeco_1_nor), .ADD(ipdeco_1_add),
    .LW(MemtoReg[0]), .ADDI(ipdeco_1_addi), .SW(MemWrite), .ADDIU(ipdeco_1_addiu), .BOE(ipdeco_1_boe),
    .BNE(Branch), .ADDU(ipdeco_1_addu), .SLT(ipdeco_1_slt), .AND(ipdeco_1_and), .SLTI(ipdeco_1_slti),
    .ANDI(ipdeco_1_andi), .SLTU(ipdeco_1_sltu), .JMP(ipdeco_1_jmp), .SLL(ipdeco_1_sll), .JAL(MemtoReg[1]),
    .SRA(ipdeco_1_sra), .JR(ipdeco_1_jr), .SRL(ipdeco_1_srl), .SYSCALL(syscallout), .SUB(ipdeco_1_sub),
    .OR(ipdeco_1_or), .ORI(ipdeco_1_ori));
  or or_1 (pcnxt[1], ipdeco_1_jmp, MemtoReg[1], ipdeco_1_jr);
  or or_2 (Bcount, ipdeco_1_boe, Branch);
  or or_3 (or_3_out, Branch, ipdeco_1_boe);
  or or_4 (pcnxt[0], or_3_out, ipdeco_1_jr);
  or or_5 (Aout, 1'b0, 1'b0, 1'b0, ipdeco_1_nor, ipdeco_1_add, ipdeco_1_addi, ipdeco_1_addiu, ipdeco_1_and, ipdeco_1_and, ipdeco_1_andi, ipdeco_1_andi, ipdeco_1_andi, ipdeco_1_sll, ipdeco_1_sra, ipdeco_1_sub, ipdeco_1_or, ipdeco_1_ori, ipdeco_1_srl);
  or or_6 (RegDst[0], ipdeco_1_boe, ipdeco_1_sll, ipdeco_1_and, ipdeco_1_slt, ipdeco_1_addu, ipdeco_1_sra, ipdeco_1_srl, ipdeco_1_add, ipdeco_1_nor, ipdeco_1_sltu, ipdeco_1_sub, ipdeco_1_or, MemWrite, Branch);
  or or_7 (mout, MemtoReg[0], MemWrite);
  or or_8 (others, ipdeco_1_addu, ipdeco_1_slt, ipdeco_1_slti, ipdeco_1_sltu, syscallout);
  or or_9 (or_9_out, ipdeco_1_srl, ipdeco_1_sra, ipdeco_1_sll);
  or or_10 (or_10_out, ipdeco_1_ori, ipdeco_1_andi);
  or or_11 (ALUSrc[1], or_10_out, or_9_out);
  or or_12 (or_12_out, ipdeco_1_addi, ipdeco_1_slti, MemWrite, ipdeco_1_addiu, MemtoReg[0]);
  or or_13 (ALUSrc[0], or_9_out, or_12_out);
  or or_14 (RegWrite, ipdeco_1_sra, ipdeco_1_ori, ipdeco_1_sub, ipdeco_1_and, ipdeco_1_slt, ipdeco_1_addu, ipdeco_1_addiu, ipdeco_1_addi, MemtoReg[0], ipdeco_1_add, ipdeco_1_nor, ipdeco_1_slti, ipdeco_1_andi, ipdeco_1_sltu, ipdeco_1_or, ipdeco_1_sll, ipdeco_1_srl, MemtoReg[1]);
  or or_15 (ALUC[3], ipdeco_1_sltu, ipdeco_1_or, ipdeco_1_ori, ipdeco_1_slti, ipdeco_1_slt, ipdeco_1_nor);
  or or_16 (ALUC[2], MemWrite, ipdeco_1_sub, ipdeco_1_add, ipdeco_1_sltu, ipdeco_1_andi, ipdeco_1_and, ipdeco_1_addu, ipdeco_1_addiu, ipdeco_1_addi, MemtoReg[0]);
  or or_17 (ALUC[1], ipdeco_1_srl, ipdeco_1_andi, ipdeco_1_slti, ipdeco_1_sub, ipdeco_1_nor, ipdeco_1_and, ipdeco_1_slt);
  or or_18 (ALUC[0], MemWrite, ipdeco_1_sra, ipdeco_1_andi, ipdeco_1_slti, ipdeco_1_and, ipdeco_1_slt, ipdeco_1_addu, ipdeco_1_addiu, ipdeco_1_addi, ipdeco_1_add, MemtoReg[0]);
  or or_19 (r1out, ipdeco_1_srl, ipdeco_1_sll, ipdeco_1_sra);

  assign RegDst[1] = MemtoReg[1];
endmodule

module regfile (
  input  [4:0] Reg1_num,
  input  [4:0] Reg2,
  input  [4:0] Write_Reg_num,
  input  [31:0] Din,
  input  Write_Enable,
  input  Clock,
  output [31:0] Reg1,
  output [31:0] Reg2_2,
  output [31:0] v0,
  output [31:0] a0,
  output [31:0] s0,
  output [31:0] s1,
  output [31:0] reg31
);

  wire demultiplexer_1_out1, demultiplexer_1_out2, demultiplexer_1_out3, demultiplexer_1_out4,
       demultiplexer_1_out5, demultiplexer_1_out6, demultiplexer_1_out7, demultiplexer_1_out8,
       demultiplexer_1_out9, demultiplexer_1_out10, demultiplexer_1_out11, demultiplexer_1_out12,
       demultiplexer_1_out13, demultiplexer_1_out14, demultiplexer_1_out15, demultiplexer_1_out16,
       demultiplexer_1_out17, demultiplexer_1_out18, demultiplexer_1_out19, demultiplexer_1_out20,
       demultiplexer_1_out21, demultiplexer_1_out22, demultiplexer_1_out23, demultiplexer_1_out24,
       demultiplexer_1_out25, demultiplexer_1_out26, demultiplexer_1_out27, demultiplexer_1_out28,
       demultiplexer_1_out29, demultiplexer_1_out30, demultiplexer_1_out31;
  wire [31:0] register_1_q, register_2_q, register_4_q, register_5_q, register_6_q, register_8_q,
       register_10_q, register_11_q, register_12_q, register_13_q, register_14_q, register_15_q,
       register_16_q, register_18_q, register_19_q, register_20_q, register_21_q, register_22_q,
       register_23_q, register_24_q, register_25_q, register_26_q, register_27_q, register_28_q,
       register_29_q, register_30_q, register_31_q;

  Demultiplexer #(.select(5), .enable("false")) demultiplexer_1 (
    .out1(demultiplexer_1_out1), .out2(demultiplexer_1_out2), .out3(demultiplexer_1_out3),
    .out4(demultiplexer_1_out4), .out5(demultiplexer_1_out5), .out6(demultiplexer_1_out6),
    .out7(demultiplexer_1_out7), .out8(demultiplexer_1_out8), .out9(demultiplexer_1_out9),
    .out10(demultiplexer_1_out10), .out11(demultiplexer_1_out11), .out12(demultiplexer_1_out12),
    .out13(demultiplexer_1_out13), .out14(demultiplexer_1_out14), .out15(demultiplexer_1_out15),
    .out16(demultiplexer_1_out16), .out17(demultiplexer_1_out17), .out18(demultiplexer_1_out18),
    .out19(demultiplexer_1_out19), .out20(demultiplexer_1_out20), .out21(demultiplexer_1_out21),
    .out22(demultiplexer_1_out22), .out23(demultiplexer_1_out23), .out24(demultiplexer_1_out24),
    .out25(demultiplexer_1_out25), .out26(demultiplexer_1_out26), .out27(demultiplexer_1_out27),
    .out28(demultiplexer_1_out28), .out29(demultiplexer_1_out29), .out30(demultiplexer_1_out30),
    .out31(demultiplexer_1_out31), .in(Write_Enable), .sel(Write_Reg_num));  // open: out0
  Register #(.width(32)) register_1 (.D({32{1'b0}}), .en(1'b1), .Q(register_1_q), .clk(1'b1), .clr(1'b0));
  Register #(.width(32)) register_2 (.D(Din), .en(demultiplexer_1_out8), .Q(register_2_q), .clk(Clock), .clr(1'b0));
  Register #(.width(32)) register_3 (.D(Din), .en(demultiplexer_1_out16), .Q(s0), .clk(Clock), .clr(1'b0));
  Register #(.width(32)) register_4 (.D(Din), .en(demultiplexer_1_out24), .Q(register_4_q), .clk(Clock), .clr(1'b0));
  Register #(.width(32)) register_5 (.D(Din), .en(demultiplexer_1_out1), .Q(register_5_q), .clk(Clock), .clr(1'b0));
  Register #(.width(32)) register_6 (.D(Din), .en(demultiplexer_1_out9), .Q(register_6_q), .clk(Clock), .clr(1'b0));
  Register #(.width(32)) register_7 (.D(Din), .en(demultiplexer_1_out17), .Q(s1), .clk(Clock), .clr(1'b0));
  Register #(.width(32)) register_8 (.D(Din), .en(demultiplexer_1_out25), .Q(register_8_q), .clk(Clock), .clr(1'b0));
  Register #(.width(32)) register_9 (.D(Din), .en(demultiplexer_1_out2), .Q(v0), .clk(Clock), .clr(1'b0));
  Register #(.width(32)) register_10 (.D(Din), .en(demultiplexer_1_out10), .Q(register_10_q), .clk(Clock), .clr(1'b0));
  Register #(.width(32)) register_11 (.D(Din), .en(demultiplexer_1_out18), .Q(register_11_q), .clk(Clock), .clr(1'b0));
  Register #(.width(32)) register_12 (.D(Din), .en(demultiplexer_1_out26), .Q(register_12_q), .clk(Clock), .clr(1'b0));
  Register #(.width(32)) register_13 (.D(Din), .en(demultiplexer_1_out3), .Q(register_13_q), .clk(Clock), .clr(1'b0));
  Register #(.width(32)) register_14 (.D(Din), .en(demultiplexer_1_out11), .Q(register_14_q), .clk(Clock), .clr(1'b0));
  Register #(.width(32)) register_15 (.D(Din), .en(demultiplexer_1_out19), .Q(register_15_q), .clk(Clock), .clr(1'b0));
  Register #(.width(32)) register_16 (.D(Din), .en(demultiplexer_1_out27), .Q(register_16_q), .clk(Clock), .clr(1'b0));
  Register #(.width(32)) register_17 (.D(Din), .en(demultiplexer_1_out4), .Q(a0), .clk(Clock), .clr(1'b0));
  Register #(.width(32)) register_18 (.D(Din), .en(demultiplexer_1_out12), .Q(register_18_q), .clk(Clock), .clr(1'b0));
  Register #(.width(32)) register_19 (.D(Din), .en(demultiplexer_1_out20), .Q(register_19_q), .clk(Clock), .clr(1'b0));
  Register #(.width(32)) register_20 (.D(Din), .en(demultiplexer_1_out28), .Q(register_20_q), .clk(Clock), .clr(1'b0));
  Register #(.width(32)) register_21 (.D(Din), .en(demultiplexer_1_out5), .Q(register_21_q), .clk(Clock), .clr(1'b0));
  Register #(.width(32)) register_22 (.D(Din), .en(demultiplexer_1_out13), .Q(register_22_q), .clk(Clock), .clr(1'b0));
  Register #(.width(32)) register_23 (.D(Din), .en(demultiplexer_1_out21), .Q(register_23_q), .clk(Clock), .clr(1'b0));
  Register #(.width(32)) register_24 (.D(Din), .en(demultiplexer_1_out29), .Q(register_24_q), .clk(Clock), .clr(1'b0));
  Register #(.width(32)) register_25 (.D(Din), .en(demultiplexer_1_out6), .Q(register_25_q), .clk(Clock), .clr(1'b0));
  Register #(.width(32)) register_26 (.D(Din), .en(demultiplexer_1_out14), .Q(register_26_q), .clk(Clock), .clr(1'b0));
  Register #(.width(32)) register_27 (.D(Din), .en(demultiplexer_1_out22), .Q(register_27_q), .clk(Clock), .clr(1'b0));
  Register #(.width(32)) register_28 (.D(Din), .en(demultiplexer_1_out30), .Q(register_28_q), .clk(Clock), .clr(1'b0));
  Register #(.width(32)) register_29 (.D(Din), .en(demultiplexer_1_out7), .Q(register_29_q), .clk(Clock), .clr(1'b0));
  Register #(.width(32)) register_30 (.D(Din), .en(demultiplexer_1_out15), .Q(register_30_q), .clk(Clock), .clr(1'b0));
  Register #(.width(32)) register_31 (.D(Din), .en(demultiplexer_1_out23), .Q(register_31_q), .clk(Clock), .clr(1'b0));
  Register #(.width(32)) register_32 (.D(Din), .en(demultiplexer_1_out31), .Q(reg31), .clk(Clock), .clr(1'b0));
  Multiplexer #(.select(5), .width(32), .enable("false")) multiplexer_1 (
    .in0(register_1_q), .in1(register_5_q), .in2(v0), .in3(register_13_q), .in4(a0), .in5(register_21_q),
    .in6(register_25_q), .in7(register_29_q), .in8(register_2_q), .in9(register_6_q), .in10(register_10_q),
    .in11(register_14_q), .in12(register_18_q), .in13(register_22_q), .in14(register_26_q),
    .in15(register_30_q), .in16(s0), .in17(s1), .in18(register_11_q), .in19(register_15_q),
    .in20(register_19_q), .in21(register_23_q), .in22(register_27_q), .in23(register_31_q),
    .in24(register_4_q), .in25(register_8_q), .in26(register_12_q), .in27(register_16_q),
    .in28(register_20_q), .in29(register_24_q), .in30(register_28_q), .in31(reg31), .out(Reg1), .sel(Reg1_num));
  Multiplexer #(.select(5), .width(32), .enable("false")) multiplexer_2 (
    .in0(register_1_q), .in1(register_5_q), .in2(v0), .in3(register_13_q), .in4(a0), .in5(register_21_q),
    .in6(register_25_q), .in7(register_29_q), .in8(register_2_q), .in9(register_6_q), .in10(register_10_q),
    .in11(register_14_q), .in12(register_18_q), .in13(register_22_q), .in14(register_26_q),
    .in15(register_30_q), .in16(s0), .in17(s1), .in18(register_11_q), .in19(register_15_q),
    .in20(register_19_q), .in21(register_23_q), .in22(register_27_q), .in23(register_31_q),
    .in24(register_4_q), .in25(register_8_q), .in26(register_12_q), .in27(register_16_q),
    .in28(register_20_q), .in29(register_24_q), .in30(register_28_q), .in31(reg31), .out(Reg2_2), .sel(Reg2));

  // Other names for the same wires on the sheet: clk = Clock; reg2_num[4:0] = Reg2; reg2_t[31:0] = Reg2_2;
  //   WE = Write_Enable; write_data[31:0] = Din

  // Notes on the sheet:
  //   输入引脚
  //   输出引脚
endmodule
