// Logisim project CS1409_U201414795_王卓焱_alu - 副本.circ as structural Verilog: 7 circuits, main circuit ALU
module ALU (
  input  [31:0] X,
  input  [31:0] Y,
  input  [3:0] AluOP,
  output Signed_Overflow,
  output UnSigned_Overflow,
  output Equal,
  output [31:0] Result,
  output [31:0] Result_2
);

  wire comparator_1_lt, comparator_2_lt, \n32bit_1_c4out溢出 , \n32bit_1_out符号pro , \n32bit_2_c4out溢出 ,
       \n32bit_2_out符号pro , not_3_out;
  wire [4:0] bitselector_1_out, bitselector_2_out, bitselector_3_out;
  wire [31:0] and_1_out, bit_extender_1_out, bit_extender_2_out, divider_1_out, divider_1_rem,
       multiplier_1_cout, multiplier_1_out, n32bit_1_outsum, n32bit_2_outsum, not_1_out, not_2_out, or_1_out,
       or_2_out, shifter_1_out, shifter_2_out, shifter_3_out, xor_1_out;

  // Probe on X
  // Probe on X
  BitSelector #(.width(32), .group(5)) bitselector_1 (.in(Y), .out(bitselector_1_out), .sel(3'b000));
  BitSelector #(.width(32), .group(5)) bitselector_2 (.in(Y), .out(bitselector_2_out), .sel(3'b000));
  assign not_1_out = ~Y;  // NOT_Gate not_1, 32 bits wide
  // Probe on Y
  // Probe on Y
  Shifter #(.width(32)) shifter_1 (.in(X), .\dist (bitselector_1_out), .out(shifter_1_out));
  Shifter #(.width(32), .shift("ar")) shifter_2 (.in(X), .\dist (bitselector_2_out), .out(shifter_2_out));
  Multiplier #(.width(32)) multiplier_1 (.a(X), .b(Y), .out(multiplier_1_out), .cout(multiplier_1_cout));  // open: cin
  Divider #(.width(32)) divider_1 (.a(X), .b(Y), .out(divider_1_out), .rem(divider_1_rem));  // open: upper
  _32BIT u_32bit_1 (
    .C0(1'b0), .\out符号PRO (\n32bit_1_out符号pro ), .\C4out溢出 (\n32bit_1_c4out溢出 ), .outsum(n32bit_1_outsum),
    .in_2(Y), .in_3(X));
  _32BIT u_32bit_2 (
    .C0(1'b1), .\out符号PRO (\n32bit_2_out符号pro ), .\C4out溢出 (\n32bit_2_c4out溢出 ), .outsum(n32bit_2_outsum),
    .in_2(X), .in_3(not_1_out));
  assign and_1_out = X & Y;  // AND_Gate and_1, 32 bits wide
  assign or_1_out = X | Y;  // OR_Gate or_1, 32 bits wide
  assign xor_1_out = X ^ Y;  // XOR_Gate xor_1, 32 bits wide
  assign or_2_out = X | Y;  // OR_Gate or_2, 32 bits wide
  Comparator #(.width(32)) comparator_1 (.a(X), .b(Y), .lt(comparator_1_lt));  // open: gt, eq
  Comparator #(.width(32), .mode("unsigned")) comparator_2 (.a(X), .b(Y), .lt(comparator_2_lt));  // open: gt, eq
  Comparator #(.width(32), .mode("unsigned")) comparator_3 (.a(X), .b(Y), .eq(Equal));  // open: gt, lt
  BitSelector #(.width(32), .group(5)) bitselector_3 (.in(Y), .out(bitselector_3_out), .sel(3'b000));
  assign not_2_out = ~or_2_out;  // NOT_Gate not_2, 32 bits wide
  assign bit_extender_1_out = {{31{1'b0}}, comparator_1_lt};  // Bit_Extender bit_extender_1
  assign bit_extender_2_out = {{31{1'b0}}, comparator_2_lt};  // Bit_Extender bit_extender_2
  // Probe on AluOP
  Shifter #(.width(32), .shift("lr")) shifter_3 (.in(X), .\dist (bitselector_3_out), .out(shifter_3_out));
  // Probe on Result
  // Probe on Result
  not not_3 (not_3_out, \n32bit_2_c4out溢出 );
  // Probe on Result_2
  Multiplexer #(.select(4)) multiplexer_1 (
    .in0(1'b0), .in1(1'b0), .in2(1'b0), .in3(1'b0), .in4(1'b0), .in5(\n32bit_1_out符号pro ),
    .in6(\n32bit_2_out符号pro ), .in7(1'b0), .in8(1'b0), .in9(1'b0), .in10(1'b0), .in11(1'b0), .in12(1'b0),
    .in13(1'b0), .in14(1'b0), .in15(1'b0), .out(Signed_Overflow), .sel(AluOP));  // open: en
  Multiplexer #(.select(4)) multiplexer_2 (
    .in0(1'b0), .in1(1'b0), .in2(1'b0), .in3(1'b0), .in4(1'b0), .in5(\n32bit_1_c4out溢出 ), .in6(not_3_out),
    .in7(1'b0), .in8(1'b0), .in9(1'b0), .in10(1'b0), .in11(1'b0), .in12(1'b0), .in13(1'b0), .in14(1'b0),
    .in15(1'b0), .out(UnSigned_Overflow), .sel(AluOP));  // open: en
  Multiplexer #(.select(4), .width(32)) multiplexer_3 (
    .in0(shifter_1_out), .in1(shifter_2_out), .in2(shifter_3_out), .in3(multiplier_1_out),
    .in4(divider_1_out), .in5(n32bit_1_outsum), .in6(n32bit_2_outsum), .in7(and_1_out), .in8(or_1_out),
    .in9(xor_1_out), .in10(not_2_out), .in11(bit_extender_1_out), .in12(bit_extender_2_out),
    .in13({32{1'b0}}), .in14({32{1'b0}}), .in15({32{1'b0}}), .out(Result), .sel(AluOP));  // open: en
  Multiplexer #(.select(4), .width(32)) multiplexer_4 (
    .in0({32{1'b0}}), .in1({32{1'b0}}), .in2({32{1'b0}}), .in3(multiplier_1_cout), .in4(divider_1_rem),
    .in5({32{1'b0}}), .in6({32{1'b0}}), .in7({32{1'b0}}), .in8({32{1'b0}}), .in9({32{1'b0}}),
    .in10({32{1'b0}}), .in11({32{1'b0}}), .in12({32{1'b0}}), .in13({32{1'b0}}), .in14({32{1'b0}}),
    .in15({32{1'b0}}), .out(Result_2), .sel(AluOP));  // open: en

  // Other names for the same wires on the sheet: OF = Signed_Overflow; Result2[31:0] = Result_2; S[3:0] = AluOP;
  //   UOF = UnSigned_Overflow

  // Notes on the sheet:
  //   不要改变此引脚区域内容，也不要改变ALU封装形式
  //   输入引脚
  //   请在下方利用上方输入输出引脚的隧道信号构建ALU电路，ctrl+d复制选择部件
  //   华中科技大学计算机学院 计算机组成原理，鸣谢加州大学伯克利CS61C课程
  //   输出引脚
  //   探测区域
endmodule

module \演示电路  (
  input  [31:0] X,
  input  [31:0] Y,
  input  [3:0] ALUOP,
  output Signed_Overflow,
  output Unsigned_overflow,
  output [31:0] Result,
  output [31:0] Result_2,
  output Equal
);

  // Probe on X
  // Probe on X
  ALU alu_1 (
    .AluOP(ALUOP), .X(X), .Equal(Equal), .Result(Result), .Signed_Overflow(Signed_Overflow), .Y(Y),
    .Result_2(Result_2), .UnSigned_Overflow(Unsigned_overflow));
  // Probe on ALUOP
  // Probe on Y
  // Probe on Y
  // Probe on Result
  // Probe on Result
  // Probe on Result_2

  // Notes on the sheet:
  //   ALu电路无需调整位置即可连接在该电路中，并且不能出现蓝色线缆和三态输出
endmodule

module \等差数列  (
  input  [31:0] \数列初始值 ,
  input  [31:0] \等差值 ,
  input  \时钟 ,
  output [31:0] Result
);

  // Probe on \数列初始值 
  // Probe on \数列初始值 
  // Probe on \等差值 
  // Probe on \等差值 
  // Probe on Result
  // Probe on Result

  // Other names for the same wires on the sheet: 数列初值[31:0] = \数列初始值 ; 累加和[31:0] = Result

  // Notes on the sheet:
  //   不要改变此引脚区域内容，也不要改变ALU封装形式
  //   请在下方利用上方输入输出引脚的隧道信号构建等差数列求和电路，ctrl+d复制选择部件
  //   华中科技大学计算机学院 计算机组成原理，鸣谢加州大学伯克利CS61C课程
  //   输出引脚
  //   探测区域
endmodule

module _4bit (
  input  in_1,
  input  [3:0] P,
  input  [3:0] in_3,
  output [5:0] out
);

  wire and_1_out, and_2_out, and_3_out, and_4_out, and_5_out, and_6_out, and_7_out, and_8_out, and_9_out,
       and_10_out, and_12_out, and_13_out, and_14_out;

  and and_1 (and_1_out, P[3], in_3[2]);
  and and_2 (and_2_out, P[3], P[2], in_3[1]);
  or or_1 (out[5], in_3[3], and_1_out, and_2_out, and_3_out, and_4_out);
  and and_3 (and_3_out, P[3], P[2], P[1], in_3[0]);
  and and_4 (and_4_out, P[3], P[2], P[1], P[0], in_1);
  and and_5 (and_5_out, P[2], in_3[1]);
  or or_2 (out[4], in_3[2], and_5_out, and_6_out, and_7_out);
  and and_6 (and_6_out, P[2], P[1], in_3[0]);
  and and_7 (and_7_out, P[2], P[1], P[0], in_1);
  or or_3 (out[3], in_3[1], and_8_out, and_9_out);
  and and_8 (and_8_out, P[1], in_3[0]);
  and and_9 (and_9_out, P[1], P[0], in_1);
  or or_4 (out[2], in_3[0], and_10_out);
  and and_10 (and_10_out, P[0], in_1);
  and and_11 (out[0], P[0], P[1], P[2], P[3]);
  and and_12 (and_12_out, P[3], P[2], P[1], in_3[0]);
  and and_13 (and_13_out, P[2], P[3], in_3[1]);
  and and_14 (and_14_out, P[3], in_3[2]);
  or or_5 (out[1], and_12_out, and_13_out, and_14_out, in_3[3]);

  // Notes on the sheet:
  //   G*P*
  //   P*
  //   C0
endmodule

module GP (
  input  [3:0] X,
  input  [3:0] Y,
  output [3:0] Gout,
  output [3:0] Pout
);

  and and_1 (Gout[3], X[3], Y[3]);
  xor xor_1 (Pout[3], X[3], Y[3]);
  and and_2 (Gout[2], X[2], Y[2]);
  xor xor_2 (Pout[2], X[2], Y[2]);
  and and_3 (Gout[1], X[1], Y[1]);
  xor xor_3 (Pout[1], Y[1], X[1]);
  and and_4 (Gout[0], X[0], Y[0]);
  xor xor_4 (Pout[0], X[0], Y[0]);
endmodule

module _4bitaLL (
  input  C0,
  input  [3:0] x,
  input  [3:0] y,
  output C4out,
  output [3:0] Sout,
  output out,
  output out_2,
  output out_3
);

  wire [3:0] gp_1_gout, gp_1_pout;
  wire [3:2] n4bit_1_out;

  xor xor_1 (Sout[3], gp_1_pout[3], out_3);
  xor xor_2 (Sout[2], gp_1_pout[2], n4bit_1_out[3]);
  _4bit u_4bit_1 (.in_1(C0), .in_3(gp_1_gout), .P(gp_1_pout), .out({C4out, out_3, n4bit_1_out, out, out_2}));
  GP gp_1 (.Gout(gp_1_gout), .Pout(gp_1_pout), .X(x), .Y(y));
  xor xor_3 (Sout[1], gp_1_pout[1], n4bit_1_out[2]);
  xor xor_4 (Sout[0], gp_1_pout[0], C0);

  // Notes on the sheet:
  //   G
  //   G*P*
  //   P
endmodule

module _32BIT (
  input  C0,
  input  [31:0] in_2,
  input  [31:0] in_3,
  output \out符号PRO ,
  output \C4out溢出 ,
  output [31:0] outsum
);

  wire n4bitall_1_out_3;
  wire [0:0] n4bit_3_out, n4bit_3_out_2;
  wire [3:0] n4bitall_4_out, n4bitall_4_out_2, n4bitall_8_out, n4bitall_8_out_2;
  wire [5:0] n4bit_1_out, n4bit_2_out;
  wire [5:2] n4bit_3_out_3;

  xor xor_1 (\out符号PRO , n4bitall_1_out_3, \C4out溢出 );
  _4bitaLL u_4bitall_1 (
    .x(in_2[31:28]), .y(in_3[31:28]), .C0(n4bit_1_out[4]), .C4out(\C4out溢出 ), .Sout(outsum[31:28]),
    .out(n4bitall_4_out[3]), .out_2(n4bitall_4_out_2[3]), .out_3(n4bitall_1_out_3));
  _4bitaLL u_4bitall_2 (
    .x(in_2[27:24]), .y(in_3[27:24]), .C0(n4bit_1_out[3]), .Sout(outsum[27:24]), .out(n4bitall_4_out[2]),
    .out_2(n4bitall_4_out_2[2]));  // open: C4out, out_3
  _4bit u_4bit_1 (.in_1(n4bit_2_out[2]), .in_3(n4bitall_4_out), .P(n4bitall_4_out_2), .out(n4bit_1_out));
  _4bitaLL u_4bitall_3 (
    .x(in_2[23:20]), .y(in_3[23:20]), .C0(n4bit_1_out[2]), .Sout(outsum[23:20]), .out(n4bitall_4_out[1]),
    .out_2(n4bitall_4_out_2[1]));  // open: C4out, out_3
  // Probe on in_2
  _4bitaLL u_4bitall_4 (
    .x(in_2[19:16]), .y(in_3[19:16]), .C0(n4bit_2_out[2]), .Sout(outsum[19:16]), .out(n4bitall_4_out[0]),
    .out_2(n4bitall_4_out_2[0]));  // open: C4out, out_3
  _4bit u_4bit_2 (
    .in_1(C0), .in_3({2'b00, n4bit_1_out[1], n4bit_3_out_2[0]}), .P({2'b00, n4bit_1_out[0], n4bit_3_out[0]}),
    .out(n4bit_2_out));
  _4bitaLL u_4bitall_5 (
    .x(in_2[15:12]), .y(in_3[15:12]), .C0(n4bit_3_out_3[4]), .Sout(outsum[15:12]), .out(n4bitall_8_out[3]),
    .out_2(n4bitall_8_out_2[3]));  // open: C4out, out_3
  _4bitaLL u_4bitall_6 (
    .x(in_2[11:8]), .y(in_3[11:8]), .C0(n4bit_3_out_3[3]), .Sout(outsum[11:8]), .out(n4bitall_8_out[2]),
    .out_2(n4bitall_8_out_2[2]));  // open: C4out, out_3
  // Probe on in_3
  _4bit u_4bit_3 (
    .in_1(C0), .in_3(n4bitall_8_out), .P(n4bitall_8_out_2),
    .out({n4bit_3_out_3, n4bit_3_out_2[0], n4bit_3_out[0]}));
  _4bitaLL u_4bitall_7 (
    .x(in_2[7:4]), .y(in_3[7:4]), .C0(n4bit_3_out_3[2]), .Sout(outsum[7:4]), .out(n4bitall_8_out[1]),
    .out_2(n4bitall_8_out_2[1]));  // open: C4out, out_3
  _4bitaLL u_4bitall_8 (
    .x(in_2[3:0]), .y(in_3[3:0]), .C0(C0), .Sout(outsum[3:0]), .out(n4bitall_8_out[0]),
    .out_2(n4bitall_8_out_2[0]));  // open: C4out, out_3
  // Probe on outsum

  // Notes on the sheet:
  //   X
  //   Y
endmodule
